// Logisim project 2part.circ as structural Verilog: 1 circuit, main circuit main
module main (
  input  A3,
  input  A2,
  input  A1,
  input  A0,
  input  B3,
  input  B2,
  input  B1,
  input  B0,
  output T3,
  output T2,
  output T1,
  output T0,
  output Y3,
  output Y2,
  output Y1,
  output Y0,
  output OVF
);

  wire AD31_out, and_2_out, and_3_out, and_4_out, and_5_out, and_6_out, and_7_out, and_8_out, BD31_out,
       C1_out, C1P1_out, C2_out, C2P2_out, C3_out, C3P3_out, C4_out, C5_out, C6_out, DA1_out, DA2_out,
       DA3_out, DB1_out, DB2_out, DB3_out, G1_out, G2_out, G3_out, K1_out, K_out, not_1_out, not_2_out,
       not_3_out, not_4_out, NZ1_out, or_2_out, P1_out, P2_out, P3_out, PZ2_out, S1_out, S2_OR_S1_out,
       S2_out, S3_out, S3S1_out, S3S2_out, U1_out, U2_out, U3_NZ1_out, U3_out, U3A_out, Z1_OR_Z0_out, Z1_out,
       Z2_out, Z3_out;

  or S2_OR_S1 (S2_OR_S1_out, S2_out, S1_out);
  and C6 (C6_out, K_out, S2_OR_S1_out);
  xor Z3 (Z3_out, C6_out, S3_out);
  xor P2 (P2_out, DA2_out, DB2_out);
  and AD31 (AD31_out, A3, A1);
  xor DA2 (DA2_out, A2, AD31_out);
  xor P1 (P1_out, DA1_out, DB1_out);
  xor S1 (S1_out, P1_out, C1_out);
  and G1 (G1_out, DA1_out, DB1_out);
  xor S2 (S2_out, P2_out, C2_out);
  and G2 (G2_out, DB2_out, DA2_out);
  and S3S2 (S3S2_out, S2_out, S3_out);
  xor PZ2 (PZ2_out, S2_out, K_out);
  or U3 (U3_out, Z3_out, U3A_out);
  xor U1 (U1_out, Z1_out, U3_out);
  and DA3 (DA3_out, A3, A2, A1);
  xor DA1 (DA1_out, A3, A1);
  xor S0 (Y0, A0, B0);
  and C1P1 (C1P1_out, P1_out, C1_out);
  or C2 (C2_out, G1_out, C1P1_out);
  and C2P2 (C2P2_out, P2_out, C2_out);
  or C3 (C3_out, G2_out, C2P2_out);
  and S3S1 (S3S1_out, S1_out, S3_out);
  or K1 (K1_out, S3S2_out, C4_out);
  or K (K_out, K1_out, S3S1_out);
  xor Z2 (Z2_out, PZ2_out, C5_out);
  and U3_NZ1 (U3_NZ1_out, U3_out, NZ1_out);
  xor U2 (U2_out, U3_NZ1_out, Z2_out);
  and BD31 (BD31_out, B3, B1);
  xor DB2 (DB2_out, B2, BD31_out);
  and C1 (C1_out, A0, B0);
  xor Z1 (Z1_out, K_out, S1_out);
  and C5 (C5_out, K_out, S1_out);
  or Z1_OR_Z0 (Z1_OR_Z0_out, Z1_out, Y0);
  and U3A (U3A_out, Z2_out, Z1_OR_Z0_out);
  not NZ1 (NZ1_out, Z1_out);
  and DB3 (DB3_out, B3, B2, B1);
  xor DB1 (DB1_out, B3, B1);
  xor P3 (P3_out, DB3_out, DA3_out);
  xor S3 (S3_out, P3_out, C3_out);
  xor xor_1 (T0, K_out, or_2_out);
  and G3 (G3_out, DB3_out, DA3_out);
  and and_1 (T1, K_out, or_2_out);
  or or_1 (OVF, or_2_out, K_out);
  and C3P3 (C3P3_out, P3_out, C3_out);
  or C4 (C4_out, G3_out, C3P3_out);
  not not_1 (not_1_out, U3_out);
  and and_2 (and_2_out, U1_out, not_1_out);
  and and_3 (and_3_out, not_1_out, not_2_out);
  not not_2 (not_2_out, U2_out);
  not not_3 (not_3_out, U1_out);
  not not_4 (not_4_out, Y0);
  and and_4 (and_4_out, not_4_out, U1_out);
  and and_5 (and_5_out, U2_out, not_3_out, not_4_out);
  or or_2 (or_2_out, U3_out, and_5_out);
  and and_6 (and_6_out, U2_out, U1_out, Y0);
  and and_7 (and_7_out, U2_out, Y0);
  and and_8 (and_8_out, not_3_out, U3_out);
  or or_3 (Y3, and_6_out, and_3_out);
  or or_4 (Y1, and_7_out, and_8_out, and_2_out);
  or or_5 (Y2, and_4_out, and_3_out);

  assign T2 = 1'b0;
  assign T3 = 1'b0;
endmodule
